// Digital circuit SPIMaster.dig as structural Verilog
module SPIMaster (
  input  nRES,
  input  MISO,
  input  D_0,
  input  D_1,
  input  D_2,
  input  D_3,
  input  D_4,
  input  D_5,
  input  D_6,
  input  D_7,
  input  nCE,
  input  A_0,
  input  RnW,
  input  VCC,
  input  GND,
  input  clk,
  output MOSI,
  output nCS_0,
  output nCS_1,
  output nCS_2,
  output nCS_3,
  output nIRQ
);

  wire and_2_out, DEN, DIV_0, DIV_1, DIV_CLK, IEN, ITC, nCTRL_RD, nCTRL_WR, nDATA_RD, nDATA_WR, not_1_out,
       nTXC, RUNNING, SEL_0, SEL_1, SPICLK, TXC;

  PowerSupply powersupply_1 (.VDD(VCC), .GND(GND));
  StateMachine statemachine_1 (.TXC(TXC), .nRES(nRES), .CLK(SPICLK), .VCC(VCC), .GND(GND));
  // DataRegister dataregister_1: pin names not known; wires that end beside it: MISO, SPICLK, nDATA_RD, nDATA_WR, TXC, MOSI, nRES, GND, VCC, D_0, D_1, D_2, D_3, D_4, D_5, D_6, D_7
  // ControlRegister controlregister_1: pin names not known; wires that end beside it: D_0, D_1, D_2, D_3, D_4, D_5, D_6, D_7, nRES, nCTRL_WR, nCTRL_RD, nDATA_WR, GND, VCC, RUNNING, DIV_0, DIV_1, SEL_0, SEL_1, DEN, IEN, ITC
  not not_1 (not_1_out, DEN);
  and and_1 (SPICLK, DIV_CLK, RUNNING);
  and and_2 (and_2_out, ITC, IEN);
  not not_2 (nTXC, TXC);
  ClockSelect clockselect_1 (.DIV0(GND), .VCC(DIV_0), .GND(DIV_1), .RES(GND));  // open: DIV1, CLK, DIV_CLK
  _74139 Device___Register_Select (
    .pin1(not_1_out), .pin2(SEL_0), .pin3(SEL_1), .pin4(nCS_0), .pin5(nCS_1), .pin6(nCS_2), .pin7(nCS_3),
    .pin8(GND), .pin9(nCTRL_RD), .pin10(nCTRL_WR), .pin11(nDATA_RD), .pin12(nDATA_WR), .pin13(A_0),
    .pin14(RnW), .pin15(nCE), .pin16(VCC));
  not not_3 (nIRQ, and_2_out);

  // Notes on the sheet:
  //   nRES: default 1
  //   nCE: default 1
  //   nCS_0: pin 4
  //   nCS_1: pin 5
  //   nCS_2: pin 6
  //   nCS_3: pin 7
  //   RnW: default 1
  //   VCC: default 1
endmodule
